# Fritzing sketch coche sonar (saved by Fritzing 0.9.3b)
breadboards: 1

parts:
  Componente1 = Arduino Uno (Rev3)
  IC1 = L293D [package=THT]
  M1 = DC Motor
  M2 = DC Motor
  Componente2 = Bluetooth HC-05 Macho
  hc-sr1 = hc-sr04

nets:
  N1: Componente1.D8, IC1.+V
  N2: Componente1.D9_PWM, IC1.In_3
  N3: Componente1.D10_PWM/SS, IC1.Enable_1
  N4: Componente1.D11_PWM/MOSI, IC1.Enable_2
  N5: Componente1.D0/RX, Componente2.TXD
  N6: Componente1.D1/TX, Componente2.RXD
  N7: Componente1.D3_PWM, hc-sr1.Trig
  N8: Componente1.D4, hc-sr1.Echo
  N9: Componente1.D6_PWM, IC1.In_1
  VCC: Componente1.D7, Componente1.5V, Componente2.VCC, hc-sr1.VCC
  GND: Componente1.GND, IC1.0V, Componente2.GND, hc-sr1.GND
  N10: IC1.Out_1_(_Controlled_by_Enable_1_), M2.pin_2
  N11: IC1.Out_2_(_Controlled_by_Enable_1_), M2.pin_1
  N12: IC1.Out_3_(_Controlled_by_Enable_2_), M1.pin_2
  N13: IC1.Out_4_(_Controlled_by_Enable_2_), M1.pin_1
